# Fritzing sketch circuit24 (saved by Fritzing 0.9.1b)
breadboards: 1

parts:
  Composant1 = Arduino Nano (Rev3.0)
  M1 = DC Motor
  IC1 = L293D [package=THT]
  VCC1 = 4 x AAA Battery Mount

nets:
  N1: Composant1.GND, M1.pin_1, IC1.0V
  N2: Composant1.D4, IC1.In_2
  N3: Composant1.D5, IC1.In_1
  N4: Composant1.D9, IC1.Enable_1
  N5: M1.pin_2, IC1.Out_1_(_Controlled_by_Enable_1_)
  N6: IC1.Out_2_(_Controlled_by_Enable_1_), VCC1.-
  N7: IC1.+Vmotor, IC1.+V, VCC1.+
